# Fritzing sketch Mouser_UV_Alert_Project_SummerSTEAM2018 (saved by Fritzing 0.9.3b)
breadboards: 1

parts:
  Part1 = SI1145 Digital UV Index + IR + Visible Light Sensor [part_number=1777]
  Part2 = Arduino MKR1000
  J1 = Piezo Speaker
  S1 = Round Pushbutton
  Q1 = NPN-Transistor [package="TO92 [THT]"]
  R1 = Resistor [tolerance=±5% resistance=1k package=THT]
  R2 = Resistor [tolerance=±5% resistance=10k package=THT]
  BATT1 = LiPoly Battery (1300mAh)  # not connected

nets:
  GND: Part1.GND, Part2.GND, Q1.E, R2.Pin_0
  +3V3: Part1.+3V3, Part2.VCC, J1.pin2, S1.leg1
  N1: Part1.SCL, Part2.D12_SCL
  N2: Part1.SDA, Part2.D11_SDA
  N3: Part2.D6, R1.Pin_0
  N4: Part2.D7, S1.leg0, R2.Pin_1
  N5: J1.pin1, Q1.C
  N6: Q1.B, R1.Pin_1

custom parts:
  SI1145 Digital UV Index + IR + Visible Light Sensor: The SI1145 is a new sensor from SiLabs with a calibrated light sensing algorithm that can calculate UV Index. It doesn't contain an actual UV sensing element, instead it approximates it based on visible & IR light from the sun. We took this outside a couple days and compared the calculated UV index with the news-reported index and found it was very accurate! It's a digital sensor that works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
  Arduino MKR1000: MKR1000 is a powerful board that combines the functionality of the Zero and the Wi-Fi Shield. It is the ideal solution for makers wanting to design IoT projects with minimal previous experience in networking
  LiPoly Battery (1300mAh): Lithium Ion Polymer Battery (1300mAh)
